# Fritzing sketch ir_tag_sketch (saved by Fritzing 1.0.1rc)
breadboards: 1

parts:
  A1 = Raspberry Pi Pico H
  OLED1 = OLED 128x64 I2C Monochrome Display
  IR3 = vs1838b [package=THT]
  LED2 = Red LED - Rect 5x2x7mm [package="5x2x7 mm [THT]"]
  LED3 = Yellow LED - Rect 5x2x7mm [package="5x2x7 mm [THT]"]
  R1 = 470 Ω Resistor [package="0402 [SMD]"]
  R2 = 470 Ω Resistor [package="0402 [SMD]"]
  LED4 = Green LED - Rect 5x2x7mm [package="5x2x7 mm [THT]"]
  R3 = Resistor Mini [tolerance=±5% resistance=220 package=THT]

nets:
  GND: A1.GND, OLED1.SCK, IR3.GND, R1.Pin_0, R2.Pin_0, R3.Pin_0
  N1: A1.GP9, OLED1.SDA
  N2: A1.GP14, OLED1.OLED_.96"
  N3: A1.GP15, IR3.Data
  N4: A1.GP18, LED4.anode
  N5: A1.GP19, LED3.anode
  N6: A1.GP20, LED2.anode
  N7: A1.VBUS, OLED1.VDD, IR3.Vs
  N8: LED2.cathode, R3.Pin_1
  N9: LED3.cathode, R2.Pin_1
  N10: R1.Pin_1, LED4.cathode

custom parts:
  Raspberry Pi Pico H: Raspberry Pi Pico H. Based around the RP2040 microcontroller the Pico H is a low cost microcontroller device bringing Raspberry Pi quality, cost, and easy of use to the microcontroller space.
  Red LED - Rect 5x2x7mm: A generic rectangular red LED (~1.8V) 5mm x 2mm x 7mm
  Yellow LED - Rect 5x2x7mm: A generic rectangular yellow LED (~1.8V) 5mm x 2mm x 7mm
  470 Ω Resistor: Resistor Basic schematic elements and footprints for 0603, 1206, and PTH resistors.
  Green LED - Rect 5x2x7mm: A generic rectangular green LED (~1.8V) 5mm x 2mm x 7mm
  Resistor Mini: A generic resistor (0.25W)
